# Fritzing sketch multiple_relais (saved by Fritzing 0.9.3b)
breadboards: 1

parts:
  Part1 = Arduino Uno (Rev3)
  U1 = 2-Channel 5v Relay Shield [package=relay-2ch5v10a]
  LED1 = smd LED [color="Red (633nm)" package="0805 [SMD]"]
  LED2 = smd LED [color="Green (555nm)" package="0805 [SMD]"]

nets:
  N1: Part1.D8, U1.IN1
  N2: Part1.D9_PWM, U1.IN2
  N3: Part1.D12/MISO, U1.K1-On, U1.K2-In, LED1.cathode
  N4: Part1.D13/SCK, U1.K1-In
  GND: Part1.GND, U1.GND, LED1.anode, LED2.anode
  5V: Part1.5V, U1.VCC
  N5: U1.K2-On, LED2.cathode

custom parts:
  2-Channel 5v Relay Shield: 2 Channel 5v Relay Shield w. 2x SPD-06VDC-SD-C
