# Fritzing sketch rpi_multiple_relais (saved by Fritzing 0.9.3b)

parts:
  U1 = 2-Channel 5v Relay Shield [package=relay-2ch5v10a]
  L1 = Bulb holder (E10) with base
  L2 = Bulb holder (E10) with base
  VCC2 = 4 x AAA Battery Mount
  VCC1 = 4 x AAA Battery Mount
  Raspberry_Pi_1 = Raspberry Pi 3 [part_number=RPI-3-V1.2]

nets:
  VCC: U1.VCC, Raspberry_Pi_1.5V
  GND: U1.GND, Raspberry_Pi_1.GND
  N1: U1.IN1, Raspberry_Pi_1.GIPO17
  N2: U1.IN2, Raspberry_Pi_1.GIPO18
  N3: U1.K1-In, VCC2.+
  N4: U1.K1-On, U1.K2-In, L2.pin_2
  N5: U1.K2-On, L1.pin_2
  N6: L1.pin_1, VCC1.-

custom parts:
  2-Channel 5v Relay Shield: 2 Channel 5v Relay Shield w. 2x SPD-06VDC-SD-C
  Bulb holder (E10) with base: A bulb holder for an E10 bulb with a base.
